# Fritzing sketch klonk (saved by Fritzing 0.9.2b)
circuit board: 4cm x 6cm
breadboards: 1

parts:
  RFID-Module = RFID-RC522-v2
  D1 = Rectifier Diode [part_number=1N4001 package="300 mil [THT]"]
  D2 = Rectifier Diode [part_number=1N4001 package="300 mil [THT]"]
  R1 = Resistor [tolerance=±5% resistance=220 package=THT]
  LED1 = LED - 5mm [color="Green (565nm)" package="5 mm [THT]"]
  Pro_Micro1 = Pro Micro
  S1 = Momentary Switch [package=ksa_sealed_tac_switch]

nets:
  N1: RFID-Module.SDA, Pro_Micro1.D2
  N2: RFID-Module.SCK, Pro_Micro1.D15/SCLK
  N3: RFID-Module.MOSI, Pro_Micro1.D16/MOSI
  N4: RFID-Module.MISO, Pro_Micro1.D14/MISO
  GND: RFID-Module.GND, LED1.cathode, Pro_Micro1.GND, S1.2
  N5: RFID-Module.RST, Pro_Micro1.D3
  N6: RFID-Module.3.3V, D2.cathode
  N7: D1.cathode, D2.anode
  N8: D1.anode, Pro_Micro1.VCC
  N9: R1.Pin_0, LED1.anode
  N10: R1.Pin_1, Pro_Micro1.D18/A0
  N11: Pro_Micro1.D19/A1, S1.1

notes:
  Klonk
  Change the following two lines in Keyboard_RFID_DE.ino (single color LED Version) Sketch:
  from:
  #define OLED 5
  to:
  #define OLED 18
  from:
  const byte buttonPin = 4;
  to:
  const byte buttonPin = 19;
  For whatever Reason Labels for GND and RST are swapped in Schematics for RFID Module.
  Change the following two lines in Keyboard_RFID_DE.ino (single color LED Version) Sketch:
  from:
  #define OLED 5
  to:
  #define OLED 18
  from:
  const byte buttonPin = 4;
  to:
  const byte buttonPin = 19;

custom parts:
  RFID-RC522-v2: A simple China made RFID-RC522 Reader; do check the pin labels, as this is a MFRC522 based clone.
  Pro Micro: The SparkFun Pro Micro is a complete USB-based microcontoller development system, in a very small footprint, capable of implementing many types of projects. All programming can be done via the USB port.
  Momentary Switch: Printtaster quadr. gelb, Raster 2.54mm 50V 50mA, 12x12x9mm Pusterla Art.Nr. 4274
