# Fritzing sketch klonk_bt (saved by Fritzing 0.9.3b)
circuit board: 4cm x 6cm
breadboards: 1

parts:
  RFID-Module = RFID-RC522-v2
  D1 = Rectifier Diode [part_number=1N4001 package="300 mil [THT]"]
  D2 = Rectifier Diode [part_number=1N4001 package="300 mil [THT]"]
  Pro_Micro1 = Pro Micro
  S1 = Momentary Switch [package=ksa_sealed_tac_switch]
  HC-05 = Bluetooth HC-05 Macho
  R2 = Resistor [tolerance=±5% resistance=220 package=THT]  # not connected
  R3 = Resistor [tolerance=±5% resistance=2.2k package=THT]
  R4 = Resistor [tolerance=±5% resistance=1k package=THT]
  S2 = Momentary Switch [package=ksa_sealed_tac_switch]  # not connected
  S3 = Momentary Switch [package=ksa_sealed_tac_switch]
  LED1 = RGB LED (com. cathode, rgb) [package="5 mm [THT]"]

nets:
  N1: RFID-Module.SDA, Pro_Micro1.D2
  N2: RFID-Module.SCK, Pro_Micro1.D15/SCLK
  N3: RFID-Module.MOSI, Pro_Micro1.D16/MOSI
  N4: RFID-Module.MISO, Pro_Micro1.D14/MISO
  GND: RFID-Module.GND, Pro_Micro1.GND, S1.2, HC-05.GND, R3.Pin_0, S3.1, LED1.common_cathode
  N5: RFID-Module.RST, Pro_Micro1.D3
  N6: RFID-Module.3.3V, D2.cathode
  N7: D1.cathode, D2.anode
  VCC: D1.anode, Pro_Micro1.VCC, HC-05.VCC, LED1.green_anode
  N8: Pro_Micro1.D6, HC-05.State
  N9: Pro_Micro1.D7, S3.2
  N10: Pro_Micro1.D9, HC-05.TXD
  N11: Pro_Micro1.D10, R4.Pin_1
  N12: Pro_Micro1.D18/A0, LED1.blue_anode
  N13: Pro_Micro1.D19/A1, S1.1
  N14: HC-05.RXD, R3.Pin_1, R4.Pin_0

notes:
  Klonk
  Change the following two lines in Keyboard_RFID_DE.ino (single color LED Version) Sketch:
  from:
  #define OLED 5
  to:
  #define OLED 18
  from:
  const byte buttonPin = 4;
  to:
  const byte buttonPin = 19;
  For whatever Reason Labels for GND and RST are swapped in Schematics for RFID Module.
  Change the following two lines in Keyboard_RFID_DE.ino (single color LED Version) Sketch:
  from:
  #define OLED 5
  to:
  #define OLED 18
  from:
  const byte buttonPin = 4;
  to:
  const byte buttonPin = 19;

custom parts:
  RFID-RC522-v2: A simple China made RFID-RC522 Reader; do check the pin labels, as this is a MFRC522 based clone.
  Pro Micro: The SparkFun Pro Micro is a complete USB-based microcontoller development system, in a very small footprint, capable of implementing many types of projects. All programming can be done via the USB port.
  Momentary Switch: Printtaster quadr. gelb, Raster 2.54mm 50V 50mA, 12x12x9mm Pusterla Art.Nr. 4274
