# Fritzing sketch klonk_rfid_rc522_rgb_led (saved by Fritzing 0.9.2b)
circuit board: 4cm x 6cm
breadboards: 1

parts:
  RFID-Module = RFID-RC522-v2
  Pro_Micro1 = Pro Micro
  S1 = Momentary Switch [package=ksa_sealed_tac_switch]
  VREG1 = Voltage Regulator [package=TO92]
  LED1 = RGB LED (shift register, rgb) [package="5 mm [THT]"]

nets (from the pcb view):
  N1: RFID-Module.SDA, Pro_Micro1.D2
  N2: RFID-Module.SCK, Pro_Micro1.D15/SCLK
  N3: RFID-Module.MOSI, Pro_Micro1.D16/MOSI
  N4: RFID-Module.MISO, Pro_Micro1.D14/MISO
  GND: RFID-Module.GND, Pro_Micro1.GND, S1.2, VREG1.GND, LED1.GND
  N5: RFID-Module.RST, Pro_Micro1.D3
  N6: RFID-Module.3.3V, VREG1.OUT
  N7: Pro_Micro1.D18/A0, LED1.DIN
  N8: Pro_Micro1.D19/A1, S1.1
  VCC: Pro_Micro1.VCC, VREG1.IN, LED1.VDD

notes:
  Change the following two lines in Keyboard_RFID_DE.ino (single color LED Version) Sketch:
  from:
  #define OLED 5
  to:
  #define OLED 18
  from:
  const byte buttonPin = 4;
  to:
  const byte buttonPin = 19;
  For whatever Reason Labels for GND and RST are swapped in Schematics for RFID Module.
  Change the following two lines in Keyboard_RFID_DE.ino (single color LED Version) Sketch:
  from:
  #define OLED 5
  to:
  #define OLED 18
  from:
  const byte buttonPin = 4;
  to:
  const byte buttonPin = 19;
  Klonk
  RFID-RC522
  RGB LED

custom parts:
  RFID-RC522-v2: A simple China made RFID-RC522 Reader; do check the pin labels, as this is a MFRC522 based clone.
  Pro Micro: The SparkFun Pro Micro is a complete USB-based microcontoller development system, in a very small footprint, capable of implementing many types of projects. All programming can be done via the USB port.
  Momentary Switch: Printtaster quadr. gelb, Raster 2.54mm 50V 50mA, 12x12x9mm Pusterla Art.Nr. 4274
  Voltage Regulator: Voltage Regulator Microchip MCP 1700 The MCP1700 is a CMOS low dropout positive voltage regulator which can source up to 250mA of current with an extremely low input-output voltage differential of 178mV at 250mA.
  RGB LED (shift register, rgb): A 5 or 8 mm RGB LED
